// Logisim project grynets.circ as structural Verilog
module ALU (
  input  [2:0] F,
  input  [31:0] B,
  input  [31:0] A,
  output [31:0] Y,
  output Zero,
  output out_6
);

  wire [31:0] adder_1_out, and_1_out, bit_extender_1_out, multiplexer_1_out, not_1_out, or_1_out;

  Multiplexer #(.width(32), .enable("false")) multiplexer_1 (
    .in0(B), .in1(not_1_out), .out(multiplexer_1_out), .sel(F[2]));
  assign not_1_out = ~B;  // NOT_Gate not_1, 32 bits wide
  Adder #(.width(32)) adder_1 (.a(multiplexer_1_out), .b(A), .out(adder_1_out), .cin(F[2]));  // open: cout
  assign and_1_out = multiplexer_1_out & A;  // AND_Gate and_1, 32 bits wide
  assign or_1_out = multiplexer_1_out | multiplexer_1_out;  // OR_Gate or_1, 32 bits wide
  BitSelector #(.width(32)) bitselector_1 (.in(adder_1_out), .out(out_6), .sel({5{1'b1}}));
  assign bit_extender_1_out = {{31{1'b0}}, out_6};  // Bit_Extender bit_extender_1
  Multiplexer #(.select(2), .width(32), .enable("false")) multiplexer_2 (
    .in0(and_1_out), .in1(or_1_out), .in2(adder_1_out), .in3(bit_extender_1_out), .out(Y), .sel(F[1:0]));
  Comparator #(.width(32), .mode("unsigned")) comparator_1 (.a(Y), .b({32{1'b0}}), .eq(Zero));  // open: gt, lt
endmodule

module Datapath (
  output [31:0] v0
);

  wire clock_1_out;
  wire [2:0] bitselector_3_out, bitselector_4_out;
  wire [7:0] adder_1_out, register_1_q, shifter_1_out;
  wire [15:0] bitselector_2_out, bitselector_5_out;
  wire [20:0] bitselector_1_out;
  wire [31:0] rom_1_data;

  Clock clock_1 (.out(clock_1_out));
  Register register_1 (.D(adder_1_out), .Q(register_1_q), .clk(clock_1_out));  // open: en, clr
  Shifter #(.shift("lr")) shifter_1 (.in(register_1_q), .\dist (3'b010), .out(shifter_1_out));
  Adder adder_1 (.a(register_1_q), .b(8'h4), .out(adder_1_out));  // open: cin, cout
  ROM #(.dataWidth(32)) rom_1 (.addr(shifter_1_out), .data(rom_1_data));  // open: sel
  BitSelector #(.width(32), .group(21)) bitselector_1 (.in(rom_1_data), .out(bitselector_1_out), .sel(1'b1));
  BitSelector #(.width(32), .group(16)) bitselector_2 (.in(rom_1_data), .out(bitselector_2_out), .sel(1'b1));
  ControlUnit controlunit_1 (.Instruction(rom_1_data));  // open: RegDst, RegWrite, ALUControl, Branch, ALUSrc, out_7
  BitSelector #(.width(21), .group(3)) bitselector_3 (.in(bitselector_1_out), .out(bitselector_3_out), .sel(3'b000));
  BitSelector #(.width(16), .group(3)) bitselector_4 (.in(bitselector_2_out), .out(bitselector_4_out), .sel(3'b000));
  BitSelector #(.width(32), .group(16)) bitselector_5 (.in(rom_1_data), .out(bitselector_5_out), .sel(1'b0));
  Bit_Extender #(.in_width(16), .out_width(32), .\type ("sign")) bit_extender_1 (.in(bitselector_5_out));  // open: out
  RegisterFile registerfile_1 (
    .A1(bitselector_3_out), .A2(bitselector_4_out), .V0(v0));  // open: CLK, WD3, WE3, RD1, RD2, A3
  Multiplexer multiplexer_1 ();  // open: in0, in1, out, sel, en
  ALU alu_1 ();  // open: F, A, Y, B, Zero, out_6

  // Notes on the sheet:
  //   contents of rom_1 (hex, n*v repeats v):
  //   20040004 20820002
  //   23-21
  //   18-16
  //   15-0
endmodule

module Tests (
  input  [31:0] in_1,
  input  [31:0] in_2,
  input  [31:0] in_3,
  output [31:0] Y,
  output [7:0] out_5,
  output [7:0] out_6,
  output [2:0] out_7,
  output [20:0] out_8,
  output [2:0] out_9,
  output [15:0] out_10,
  output [2:0] out_11,
  output [15:0] out_12
);

  BitSelector #(.width(32), .group(21)) bitselector_1 (.in(in_1), .out(out_8), .sel(1'b1));
  BitSelector #(.width(32), .group(16)) bitselector_2 (.in(in_2), .out(out_10), .sel(1'b1));
  BitSelector #(.width(32), .group(16)) bitselector_3 (.in(in_3), .out(out_12), .sel(1'b0));
  BitSelector #(.width(32), .group(8)) bitselector_4 (.in(32'h12356789), .out(out_5), .sel(2'b01));
  BitSelector #(.width(32), .group(8)) bitselector_5 (.in(32'h12356789), .out(out_6), .sel(2'b01));
  BitSelector #(.group(3)) bitselector_6 (.in(out_6), .out(out_7), .sel(2'b00));
  BitSelector #(.width(21), .group(3)) bitselector_7 (.in(out_8), .out(out_9), .sel(3'b000));
  BitSelector #(.width(16), .group(3)) bitselector_8 (.in(out_10), .out(out_11), .sel(3'b000));

  assign Y = 32'hf4010207;

  // Notes on the sheet:
  //   binary values in Logisim. Convince yourself how the bits are displayed.
  //   Example 2: The bit selector is configured to have 32  
  //   bit group #1 (starting at index 0) is selected for the output.
  //   That is, the 8 bits 0x67 at bit indices 15..8  are sent to the output.
  //   Example 3: Now, assume that you want to extract 3 bits at   
  //   Example 1: A simple example that illustrates how 32-bit values are displayed as 
  //   input bits and 8 output bits. The parameter constant is 1, which means that   
  //   bit indices 10..8. This can be accoplished by putting two bit selecotrs in series.
endmodule

module RegisterFile (
  input  CLK,
  input  [2:0] A1,
  input  [31:0] WD3,
  input  [2:0] A2,
  input  WE3,
  input  [2:0] A3,
  output [31:0] RD1,
  output [31:0] RD2,
  output [31:0] V0
);

  wire and_1_out, and_2_out, and_3_out, and_4_out, and_5_out, and_6_out, and_7_out, decoder_1_out0,
       decoder_1_out1, decoder_1_out2, decoder_1_out3, decoder_1_out4, decoder_1_out5, decoder_1_out6,
       decoder_1_out7;
  wire [31:0] register_1_q, register_2_q, register_4_q, register_5_q, register_6_q, register_7_q,
       register_8_q;

  Decoder #(.select(3)) decoder_1 (
    .out0(decoder_1_out0), .out1(decoder_1_out1), .out2(decoder_1_out2), .out3(decoder_1_out3),
    .out4(decoder_1_out4), .out5(decoder_1_out5), .out6(decoder_1_out6), .out7(decoder_1_out7), .sel(A3));  // open: en
  and and_1 (and_1_out, WE3, decoder_1_out1);
  and and_2 (and_2_out, WE3, decoder_1_out2);
  and and_3 (and_3_out, WE3, decoder_1_out3);
  and and_4 (and_4_out, WE3, decoder_1_out4);
  and and_5 (and_5_out, WE3, decoder_1_out5);
  and and_6 (and_6_out, WE3, decoder_1_out6);
  and and_7 (and_7_out, WE3, decoder_1_out7);
  Register #(.width(32)) register_1 (.D({32{1'b0}}), .en(decoder_1_out0), .Q(register_1_q), .clk(CLK));  // open: clr
  Register #(.width(32)) register_2 (.D(WD3), .en(and_1_out), .Q(register_2_q), .clk(CLK));  // open: clr
  Register #(.width(32)) register_3 (.D(WD3), .en(and_2_out), .Q(V0), .clk(CLK));  // open: clr
  Register #(.width(32)) register_4 (.D(WD3), .en(and_3_out), .Q(register_4_q), .clk(CLK));  // open: clr
  Register #(.width(32)) register_5 (.D(WD3), .en(and_4_out), .Q(register_5_q), .clk(CLK));  // open: clr
  Register #(.width(32)) register_6 (.D(WD3), .en(and_5_out), .Q(register_6_q), .clk(CLK));  // open: clr
  Register #(.width(32)) register_7 (.D(WD3), .en(and_6_out), .Q(register_7_q), .clk(CLK));  // open: clr
  Register #(.width(32)) register_8 (.D(WD3), .en(and_7_out), .Q(register_8_q), .clk(CLK));  // open: clr
  Multiplexer #(.select(3), .width(32)) multiplexer_1 (
    .in0(register_1_q), .in1(register_2_q), .in2(V0), .in3(register_4_q), .in4(register_5_q),
    .in5(register_6_q), .in6(register_7_q), .in7(register_8_q), .out(RD1), .sel(A1));  // open: en
  Multiplexer #(.select(3), .width(32)) multiplexer_2 (
    .in0(register_1_q), .in1(register_2_q), .in2(V0), .in3(register_4_q), .in4(register_5_q),
    .in5(register_6_q), .in6(register_7_q), .in7(register_8_q), .out(RD2), .sel(A2));  // open: en
endmodule

module ControlUnit (
  input  [31:0] Instruction,
  output RegDst,
  output RegWrite,
  output ALUSrc,
  output Branch,
  output [2:0] ALUControl,
  output [5:0] out_7
);

  wire [31:0] shifter_1_out;

  Shifter #(.width(32), .shift("lr")) shifter_1 (.in(Instruction), .\dist (5'b11010), .out(shifter_1_out));
  BitSelector #(.width(32), .group(6)) bitselector_1 (
    .in(shifter_1_out), .out({out_7[5:3], ALUControl[2], out_7[1], ALUControl[0]}), .sel(3'b000));
  Comparator #(.width(6), .mode("unsigned")) comparator_1 (
    .a({out_7[5:3], ALUControl[2], out_7[1], ALUControl[0]}), .b(6'b001000), .eq(ALUSrc));  // open: gt, lt
  Comparator #(.width(6), .mode("unsigned")) comparator_2 (
    .a({out_7[5:3], ALUControl[2], out_7[1], ALUControl[0]}), .b({6{1'b0}}), .eq(RegDst));  // open: gt, lt
  Comparator #(.width(6), .mode("unsigned")) comparator_3 (
    .a({out_7[5:3], ALUControl[2], out_7[1], ALUControl[0]}), .b(6'b000100), .eq(Branch));  // open: gt, lt
  not not_1 (ALUControl[1], out_7[1]);
  or or_1 (RegWrite, ALUSrc, RegDst);

  assign {out_7[2], out_7[0]} = {ALUControl[2], ALUControl[0]};

  // Notes on the sheet:
  //   Skiftar bort allt förutom op
  //   Addi
  //   R-type
  //   Beq
endmodule
